# Fritzing sketch schematic (saved by Fritzing 0.9.2b)

parts:
  Part1 = Adafruit Flora [part_number="Adafruit #659"]
  Part2 = Flora Bluetooth LE

nets:
  +3V3: Part1.+3V3, Part2.3.3V
  GND: Part1.GND, Part2.GND
  N1: Part1.IO0/RX, Part2.RXI
  N2: Part1.IO1/TX, Part2.TXO

notes:
  Flora Bluetooth NeoPixel

custom parts:
  Adafruit Flora: FLORA is Adafruit's fully-featured wearable electronics platform. It's a round, sewable, Arduino-compatible microcontroller designed to empower amazing wearables projects. The FLORA is small (1.75" diameter, weighing 4.4 grams). The FLORA has built-in USB support. Built in USB means you plug it in to program it, it just shows up - all you need is a Micro-B USB cable, no additional purchases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
  Flora Bluetooth LE: The Flora Bluefruit LE makes it easy to add Bluetooth Low Energy connectivity to your Flora. Using our Bluefruit iOS App or Android App, you can quickly get your interactive project prototyped by using your iOS or Android phone/tablet as a controller.
