# Fritzing sketch schematic (saved by Fritzing 0.9.2b)

parts:
  Part1 = Adafruit Flora [part_number="Adafruit #659"]
  Part2 = Flora TCS34725 Color Sensor
  LED1 = prefix0000
  S1 = Round Pushbutton

nets:
  +3V3: Part1.+3V3, Part2.3.3V
  N1: Part1.IO6, LED1.connector2
  GND: Part1.GND, Part2.GND, LED1.connector3, S1.leg1
  N2: Part1.IO10, S1.leg0
  N3: Part1.IO2/SDA, Part2.SCL_3V
  N4: Part1.IO3/SCL, Part2.SDA_3V
  N5: Part1.VBAT, LED1.connector1

notes:
  Flora Color Sensor

custom parts:
  Adafruit Flora: FLORA is Adafruit's fully-featured wearable electronics platform. It's a round, sewable, Arduino-compatible microcontroller designed to empower amazing wearables projects. The FLORA is small (1.75" diameter, weighing 4.4 grams). The FLORA has built-in USB support. Built in USB means you plug it in to program it, it just shows up - all you need is a Micro-B USB cable, no additional purchases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
  Flora TCS34725 Color Sensor: Your electronics can now see in dazzling color with this lovely color light sensor. We found the best color sensor on the market, the TCS34725, which has RGB and Clear light sensing elements. An IR blocking filter, integrated on-chip and localized to the color sensing photodiodes, minimizes the IR spectral component of the incoming light and allows color measurements to be made accurately. The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
