# Fritzing sketch schematic (saved by Fritzing 0.9.2b)

parts:
  Part1 = GEMMA v2
  LED1 = prefix0000
  Part2 = Flora LSM303 Compass+Accel

nets:
  3.3V: Part1.3.3V, Part2.3.3V
  N1: Part1.B0, Part2.SDA
  N2: Part1.B1, LED1.connector2
  N3: Part1.B2, Part2.SCL
  GND: Part1.GND, LED1.connector3, Part2.GND
  N4: Part1.Vout, LED1.connector1

notes:
  Gemma Accelerometer

custom parts:
  GEMMA v2: Love FLORA but want a bite-sized version? Look no further, GEMMA is a tiny wearable platform board with a lot of might in a 1" diameter package. Powered by a Attiny85 and programmable with an Arduino IDE over USB, you'll be able to realize any wearable project! We wanted to design a microcontroller board that was small enough to fit into any project, and low cost enough to use without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
  Flora LSM303 Compass+Accel: Add motion and direction sensing to your wearable FLORA project with this high precision 3-axis Accelerometer+Compass sensor. Inside are two sensors, one is a classic 3-axis accelerometer, which can tell you which direction is down towards the Earth (by measuring gravity) or how fast the board is accelerating in 3D space. The other is a magnetometer that can sense where the strongest magnetic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
