# Fritzing sketch schematic (saved by Fritzing 0.9.2b)

parts:
  Part1 = GEMMA v2
  Part4 = Flora TSL2561 Lux Sensor
  Part5 = LED Sequin - Warm White [part_number=1758]

nets:
  3.3V: Part1.3.3V, Part4.3.3V
  N1: Part1.B0, Part4.SDA
  N2: Part1.B1, Part5.+
  N3: Part1.B2, Part4.SCL
  GND: Part1.GND, Part4.GND, Part5.-

notes:
  Gemma Light Sensor

custom parts:
  GEMMA v2: Love FLORA but want a bite-sized version? Look no further, GEMMA is a tiny wearable platform board with a lot of might in a 1" diameter package. Powered by a Attiny85 and programmable with an Arduino IDE over USB, you'll be able to realize any wearable project! We wanted to design a microcontroller board that was small enough to fit into any project, and low cost enough to use without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
  Flora TSL2561 Lux Sensor: Add light-reactive sensing to your wearable Flora project with this high precision Lux sensor. The TSL2561 luminosity sensor is an advanced digital light sensor, ideal for use in a wide range of light situations. Compared to low cost CdS cells, this sensor is more precise, allowing for exact lux calculations and can be configured for different gain/timing ranges to detect light ranges from up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
  LED Sequin - Warm White: Sew a little sparkle into your wearable project with an Adafruit LED Sequin. Simply connect 3 to 6VDC to the + pin and ground to the - pin, and the LED on the board will light up. You can make the LEDs fade and twinkle by using PWM.
