# Fritzing sketch schematic (saved by Fritzing 0.9.2b)

parts:
  Part1 = GEMMA v2
  LED1 = prefix0000
  Part3 = Flora SI1145 UV Sensor

nets:
  3.3V: Part1.3.3V, Part3.3.3V
  N1: Part1.B0, Part3.SDA
  N2: Part1.B1, LED1.connector2
  N3: Part1.B2, Part3.SCL
  GND: Part1.GND, LED1.connector3, Part3.GND
  N4: Part1.Vout, LED1.connector1

notes:
  Gemma UV Sensor

custom parts:
  GEMMA v2: Love FLORA but want a bite-sized version? Look no further, GEMMA is a tiny wearable platform board with a lot of might in a 1" diameter package. Powered by a Attiny85 and programmable with an Arduino IDE over USB, you'll be able to realize any wearable project! We wanted to design a microcontroller board that was small enough to fit into any project, and low cost enough to use without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
  Flora SI1145 UV Sensor: Your wearable can now keep you from getting sunburnt, with the Flora digital UV index sensor. We took our popular SI1145 UV index sensor and cut out everything you don't need for using with a Flora. It's small, round, and connects to the I2C bus pads. Flora can even use our library code to get calibrated light level and UV index data from the sensor. Please note: this sensor can be used by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
